// Digital circuit LeftRightShift.dig as structural Verilog
module LeftRightShift (
  input  [15:0] A,
  input  [3:0] Switch,
  input  Left_Right,
  output [15:0] Q
);

  wire add_1_c_o;
  wire [3:0] add_1_s, multiplexer_3_out, not_1_out;
  wire [15:0] multiplexer_1_out, multiplexer_2_out, multiplexer_5_out;
  wire [18:0] multiplexer_4_out;

  assign not_1_out = ~Switch;  // Not not_1, 4 bits wide
  Multiplexer #(.Bits(16)) multiplexer_1 (.sel(Left_Right), .in_0(A), .in_1({16{1'b0}}), .out(multiplexer_1_out));
  Multiplexer #(.Bits(16)) multiplexer_2 (.sel(Left_Right), .in_0({16{1'b0}}), .in_1(A), .out(multiplexer_2_out));
  Multiplexer #(.Bits(4)) multiplexer_3 (.sel(Left_Right), .in_0(Switch), .in_1(not_1_out), .out(multiplexer_3_out));
  Add #(.Bits(4)) add_1 (.a(4'b0000), .b(multiplexer_3_out), .c_i(Left_Right), .s(add_1_s), .c_o(add_1_c_o));
  Multiplexer #(.Selector_Bits(2), .Bits(19)) multiplexer_4 (
    .sel(add_1_s[3:2]), .in_0({multiplexer_2_out[2:0], multiplexer_1_out}),
    .in_1({multiplexer_2_out[6:0], multiplexer_1_out[15:4]}),
    .in_2({multiplexer_2_out[10:0], multiplexer_1_out[15:8]}),
    .in_3({multiplexer_2_out[14:0], multiplexer_1_out[15:12]}), .out(multiplexer_4_out));
  Multiplexer #(.Selector_Bits(2), .Bits(16)) multiplexer_5 (
    .sel(add_1_s[1:0]), .in_0(multiplexer_4_out[15:0]), .in_1(multiplexer_4_out[16:1]),
    .in_2(multiplexer_4_out[17:2]), .in_3(multiplexer_4_out[18:3]), .out(multiplexer_5_out));
  Multiplexer #(.Bits(16)) multiplexer_6 (.sel(add_1_c_o), .in_0(multiplexer_5_out), .in_1(multiplexer_2_out), .out(Q));
endmodule

/* Test case:
A	Left/Right	Switch	Q
13 	   0		   2    3
121 	   1		   4    1936
88 	   0		   3    11
6	   1               2    24
*/
