// Digital circuit reg_file.dig as structural Verilog
module reg_file (
  input  [2:0] RS1,
  input  [2:0] RS2,
  input  [2:0] WS,
  input  WE,
  input  [15:0] IN,
  input  clk,
  input  [15:0] FLAG,
  input  Fenable,
  input  Seth,
  input  [7:0] IMM8,
  output [15:0] OUT1,
  output [15:0] OUT2,
  output [15:0] PC,
  output [15:0] Frout
);

  wire and_1_out, and_2_out, and_3_out, and_4_out, and_5_out, and_6_out, and_7_out, decoder_1_out_0,
       decoder_1_out_1, decoder_1_out_2, decoder_1_out_3, decoder_1_out_4, decoder_1_out_5, decoder_1_out_7;
  wire [15:0] A, and_8_out, multiplexer_1_out, or_1_out, plus_1_s, R0_q, R1_q, R2_q, R3_q, R4_q, R5_q;

  Decoder #(.Selector_Bits(3)) decoder_1 (
    .sel(WS), .out_0(decoder_1_out_0), .out_1(decoder_1_out_1), .out_2(decoder_1_out_2),
    .out_3(decoder_1_out_3), .out_4(decoder_1_out_4), .out_5(decoder_1_out_5), .out_7(decoder_1_out_7));  // open: out_6
  and and_1 (and_1_out, WE, decoder_1_out_0);
  and and_2 (and_2_out, WE, decoder_1_out_1);
  and and_3 (and_3_out, WE, decoder_1_out_2);
  and and_4 (and_4_out, WE, decoder_1_out_3);
  and and_5 (and_5_out, WE, decoder_1_out_4);
  and and_6 (and_6_out, WE, decoder_1_out_5);
  and and_7 (and_7_out, WE, decoder_1_out_7);
  Multiplexer #(.Bits(16)) multiplexer_1 (.sel(and_7_out), .in_0(plus_1_s), .in_1(A), .out(multiplexer_1_out));
  Register #(.Bits(16), .isProgramCounter("true")) R0 (.D(A), .C(clk), .en(and_1_out), .Q(R0_q));
  Register #(.Bits(16), .isProgramCounter("true")) R1 (.D(A), .C(clk), .en(and_2_out), .Q(R1_q));
  Register #(.Bits(16), .isProgramCounter("true")) R2 (.D(A), .C(clk), .en(and_3_out), .Q(R2_q));
  Register #(.Bits(16), .isProgramCounter("true")) R3 (.D(A), .C(clk), .en(and_4_out), .Q(R3_q));
  Register #(.Bits(16), .isProgramCounter("true")) R4 (.D(A), .C(clk), .en(and_5_out), .Q(R4_q));
  Register #(.Bits(16), .isProgramCounter("true")) R5 (.D(A), .C(clk), .en(and_6_out), .Q(R5_q));
  Register #(.Bits(16), .isProgramCounter("true")) u_PC (.D(multiplexer_1_out), .C(clk), .en(1'b1), .Q(PC));
  Register #(.Bits(16), .isProgramCounter("true")) FL (.D(FLAG), .C(clk), .en(Fenable), .Q(Frout));
  assign and_8_out = {16{1'b0}} & R0_q;  // And and_8, 16 bits wide
  Add #(.Bits(16)) plus_1 (.a(16'h1), .b(PC), .c_i(1'b0), .s(plus_1_s));  // open: c_o
  Multiplexer #(.Selector_Bits(3), .Bits(16)) multiplexer_2 (
    .sel(RS1), .in_0(and_8_out), .in_1(R1_q), .in_2(R2_q), .in_3(R3_q), .in_4(R4_q), .in_5(Frout),
    .in_6(R5_q), .in_7(PC), .out(OUT1));
  Multiplexer #(.Selector_Bits(3), .Bits(16)) multiplexer_3 (
    .sel(RS2), .in_0(and_8_out), .in_1(R1_q), .in_2(R2_q), .in_3(R3_q), .in_4(R4_q), .in_5(Frout),
    .in_6(R5_q), .in_7(PC), .out(OUT2));
  assign or_1_out = OUT1 | OUT2;  // Or or_1, 16 bits wide
  Multiplexer #(.Bits(16)) multiplexer_4 (.sel(Seth), .in_0(IN), .in_1({IMM8, or_1_out[7:0]}), .out(A));

  // Other names for the same wires on the sheet: B = clk; C[2:0] = RS1; D[2:0] = RS2; Input[15:0] = IN

  // Notes on the sheet:
  //   RS1: The index of the register which should output its value to OUT1.
  //   RS2: The index of the register which should output its value to OUT2.
  //   WS: The index of the register which should save the value on IN on the next clock cycle (if WE is high).
  //   WE: Whether the register selected by WS should save the value from IN on the next cycle.
  //   IN: The value to be saved into the register specified by WS if WE is high,
  //   OUT1: The value in the register specified by RS1.
  //   OUT2: The value in the register specified by RS2.
  //   FLAG: The index of the register which should save the value on IN on the next clock cycle (if WE is high).
  //   Fenable: The index of the register which should save the value on IN on the next clock cycle (if WE is high).
  //   Seth: The index of the register which should save the value on IN on the next clock cycle (if WE is high).
  //   IMM8: The index of the register which should save the value on IN on the next clock cycle (if WE is high).
endmodule

/* Test case:
clk RS1 RS2 WS WE IN OUT1 OUT2
c 0 0 0 1 0x1234 0x0000 0x0000
c 1 0 1 1 0xBEEF 0xBEEF 0x0000
c 2 1 2 1 0xDEAD 0xDEAD 0xBEEF
c 3 2 3 1 0xFFFF 0xFFFF 0xDEAD
c 3 2 3 0 0xABCD 0xFFFF 0xDEAD
c 3 2 2 0 0xABCD 0xFFFF 0xDEAD
c 1 0 1 0 0xABCD 0xBEEF 0x0000
c 1 0 0 0 0xABCD 0xBEEF 0x0000
c 1 0 2 1 0xBADE 0xBEEF 0x0000
c 0 2 2 1 0xBADE 0x0000 0xBADE
c 0 0 2 0 0x1234 0x0000 0x0000
c 2 3 0 1 0x0000 0xBADE 0xFFFF
c 0 0 2 0 0x1234 0x0000 0x0000
*/
